# Fritzing sketch laser_toy (saved by Fritzing 0.8.7b)
circuit board: 8.46667cm x 5.64444cm
breadboards: 1

parts:
  S1 = Pushbutton [package="[THT]"]
  S2 = Pushbutton [package="[THT]"]
  Part1 = Arduino Pro
  R1 = Rotary Potentiometer (Small) [maximum_resistance=100kΩ package=THT]
  LED2 = LED - 5mm [color="Red (633nm)" package="5 mm [THT]"]
  J2 = Basic Servo
  J1 = Basic Servo
  LED1 = LED - 5mm [color="Red (633nm)" package="5 mm [THT]"]
  LED4 = LED - 5mm [color="Red (633nm)" package="5 mm [THT]"]
  LED3 = LED - 5mm [color="Red (633nm)" package="5 mm [THT]"]

nets:
  VCC: S1.Pin_1, S1.Pin_2, S2.Pin_1, S2.Pin_2, Part1.VCC, R1.leg1, J2.vcc, J1.vcc
  N1: S1.Pin_3, S1.Pin_4, Part1.D7
  N2: S2.Pin_3, S2.Pin_4, Part1.D8
  N3: Part1.D3_PWM, LED4.cathode
  N4: Part1.D4/A6, LED3.cathode
  N5: Part1.D5_PWM, LED2.cathode
  N6: Part1.D6_PWM, LED1.cathode
  N7: Part1.A0, R1.wiper
  N8: Part1.D9_PWM, J2.pulse
  N9: Part1.D10_PWM/SS, J1.pulse
  GND: Part1.GND, LED2.anode, J2.gnd, J1.gnd, LED1.anode, LED4.anode, LED3.anode
